// Logisim project LAB3.circ as structural Verilog: 2 circuits, main circuit main
module main (
  input  in2,
  input  in1,
  input  in0,
  output f7,
  output f6,
  output f5,
  output f4,
  output f3,
  output f2,
  output f1,
  output f0,
  output n1,
  output n0
);

  wire and_6_out, and_7_out, not_1_out, not_2_out, not_3_out, not_4_out, not_5_out, not_6_out;

  not not_1 (not_1_out, in1);
  not not_2 (not_2_out, in1);
  not not_3 (not_3_out, in0);
  not not_4 (not_4_out, in1);
  not not_5 (not_5_out, in0);
  not not_6 (not_6_out, in1);
  and and_1 (f7, in2, in1, in0);
  and and_2 (f6, in2, in1, in0);
  and and_3 (f5, in2, in1);
  and and_4 (f4, in2, in1, in0);
  and and_5 (f2, in2, not_1_out, in0);
  and and_6 (and_6_out, in2, not_2_out, in0);
  or or_1 (f1, and_6_out, and_7_out);
  and and_7 (and_7_out, in2, in1, not_3_out);
  and and_8 (f0, in2, not_4_out, not_5_out);
  and and_9 (n1, in1, in0);
  and and_10 (n0, not_6_out, in0);

  assign f3 = 1'b0;
endmodule

module \Задание_2  (
  input  in2,
  input  in1,
  input  in0,
  output f7,
  output f6,
  output f1,
  output f5,
  output f4,
  output f3,
  output f2,
  output f0,
  output n0
);

  wire and_1_out, and_2_out, and_3_out, and_4_out, and_5_out, and_6_out, and_7_out, and_8_out, and_9_out,
       and_10_out, and_11_out, not_1_out, not_2_out, not_3_out, not_4_out, not_5_out, not_6_out, not_7_out,
       not_8_out, not_9_out;

  and and_1 (and_1_out, in1, in0);
  and and_2 (and_2_out, in2, in1);
  not not_1 (not_1_out, in1);
  and and_3 (and_3_out, not_1_out, in0);
  not not_2 (not_2_out, in2);
  and and_4 (and_4_out, not_2_out, in1, not_3_out);
  not not_3 (not_3_out, in0);
  and and_5 (and_5_out, in2, not_4_out);
  not not_4 (not_4_out, in1);
  and and_6 (and_6_out, in2, in0);
  not not_5 (not_5_out, in2);
  and and_7 (and_7_out, not_5_out, not_6_out);
  not not_6 (not_6_out, in0);
  not not_7 (not_7_out, in2);
  and and_8 (and_8_out, not_7_out, in1);
  and and_9 (and_9_out, in1, not_8_out);
  not not_8 (not_8_out, in0);
  not not_9 (not_9_out, in1);
  and and_10 (and_10_out, in2, not_9_out, in0);
  and and_11 (and_11_out, in2, in0);
  or or_1 (n0, and_1_out, and_11_out, and_2_out);
  or or_2 (f1, and_3_out, and_4_out, and_5_out, and_6_out);
  or or_3 (f0, and_7_out, and_8_out, and_9_out, and_10_out);

  assign f2 = 1'b0;
  assign f3 = 1'b0;
  assign f4 = 1'b0;
  assign f5 = 1'b0;
  assign f6 = 1'b0;
  assign f7 = 1'b0;
endmodule
