// Logisim project RS-триггер.circ as structural Verilog: 6 circuits, main circuit main
module main (
  input  R,
  input  S,
  output Q,
  output Q_
);

  nor nor_1 (Q, R, Q_);
  nor nor_2 (Q_, Q, S);
endmodule

module \Асинхронный_RS_триггер_с_инверсными_входами  (
  output Q,
  output Q_
);

  wire clock_1_out, clock_2_out;

  Clock systemclock ();  // open: out
  Clock clock_1 (.out(clock_1_out));
  Clock clock_2 (.out(clock_2_out));
  nand \nand  (Q, clock_1_out, Q_);
  nand nand_2 (Q_, Q, clock_2_out);
endmodule

module \Синхронный_RS_триггер  (
  input  in_1,
  input  in_2,
  output out_3,
  output out_4
);

  wire clock_1_out, nand_1_out, nand_2_out;

  Clock clock_1 (.out(clock_1_out));
  nand nand_1 (nand_1_out, in_1, clock_1_out);
  nand nand_2 (nand_2_out, clock_1_out, in_2);
  nand nand_3 (out_3, nand_1_out, out_4);
  nand nand_4 (out_4, out_3, nand_2_out);
endmodule

module \S_триггер  (
  output Q,
  output Q_
);

  wire clock_1_out, clock_2_out, nand_2_out, nand_out;

  Clock clock_1 (.out(clock_1_out));
  Clock clock_2 (.out(clock_2_out));
  nand \nand  (nand_out, clock_1_out, clock_1_out);
  nand nand_2 (nand_2_out, nand_out, clock_2_out);
  nand nand_3 (Q, nand_out, Q_);
  nand nand_4 (Q_, Q, nand_2_out);
endmodule

module \R__триггер  (
  output Q,
  output Q_
);

  wire clock_1_out, clock_2_out, nand_2_out, nand_out;

  Clock clock_1 (.out(clock_1_out));
  Clock clock_2 (.out(clock_2_out));
  nand \nand  (nand_out, clock_1_out, nand_2_out);
  nand nand_2 (nand_2_out, clock_2_out, clock_2_out);
  nand nand_3 (Q, nand_out, Q_);
  nand nand_4 (Q_, Q, nand_2_out);
endmodule

module \E_триггер  (
  output Q,
  output Q_
);

  wire clock_1_out, clock_2_out, nand_2_out, nand_3_out, nand_4_out, nand_out;

  Clock clock_1 (.out(clock_1_out));
  Clock clock_2 (.out(clock_2_out));
  nand \nand  (nand_out, clock_1_out, clock_1_out);
  nand nand_2 (nand_2_out, clock_2_out, clock_2_out);
  nand nand_3 (nand_3_out, clock_1_out, nand_2_out);
  nand nand_4 (nand_4_out, nand_out, clock_2_out);
  nand nand_5 (Q, nand_3_out, Q_);
  nand nand_6 (Q_, Q, nand_4_out);
endmodule
