// Logisim project LAB6.circ as structural Verilog: 4 circuits, main circuit main
module main (
  input  X1,
  input  X2,
  output Y
);

  wire and_1_out, and_2_out, not_1_out, not_2_out;

  not not_1 (not_1_out, X1);
  not not_2 (not_2_out, X2);
  and and_1 (and_1_out, not_1_out, X2);
  and and_2 (and_2_out, X1, not_2_out);
  or or_1 (Y, and_1_out, and_2_out);
endmodule

module \Полусумматор  (
  input  X1,
  input  X2,
  output out_3,
  output out_4
);

  main main_1 (.X1(X1), .X2(X2), .Y(out_4));
  and and_1 (out_3, X1, X2);
endmodule

module \Полный_сумматор  (
  input  in_1,
  input  in_2,
  input  in_3,
  output out_4,
  output out_5
);

  wire \полусумматор_1_out_3 , \полусумматор_1_out_4 , \полусумматор_2_out_3 ;

  \Полусумматор  \u_полусумматор_1  (
    .X1(in_1), .X2(in_2), .out_3(\полусумматор_1_out_3 ), .out_4(\полусумматор_1_out_4 ));
  \Полусумматор  \u_полусумматор_2  (
    .X1(\полусумматор_1_out_4 ), .X2(in_3), .out_3(\полусумматор_2_out_3 ), .out_4(out_5));
  or or_1 (out_4, \полусумматор_1_out_3 , \полусумматор_2_out_3 );
endmodule

module \Схема_4_х_сумматоров  (
  input  X4,
  input  Y4,
  input  X3,
  input  Y3,
  input  X2,
  input  Y2,
  input  X1,
  input  Y1,
  input  P0,
  output S5,
  output S4,
  output S3,
  output S2,
  output S1
);

  wire \полный_сумматор_1_out_4 , \полный_сумматор_2_out_4 , \полный_сумматор_3_out_4 ;

  \Полный_сумматор  \u_полный_сумматор_1  (
    .in_1(X1), .in_2(Y1), .in_3(P0), .out_4(\полный_сумматор_1_out_4 ), .out_5(S1));
  \Полный_сумматор  \u_полный_сумматор_2  (
    .in_1(X2), .in_2(Y2), .in_3(\полный_сумматор_1_out_4 ), .out_4(\полный_сумматор_2_out_4 ), .out_5(S2));
  \Полный_сумматор  \u_полный_сумматор_3  (
    .in_1(X3), .in_2(Y3), .in_3(\полный_сумматор_2_out_4 ), .out_4(\полный_сумматор_3_out_4 ), .out_5(S3));
  \Полный_сумматор  \u_полный_сумматор_4  (
    .in_1(X4), .in_2(Y4), .in_3(\полный_сумматор_3_out_4 ), .out_4(S5), .out_5(S4));
endmodule
