// Logisim project Lab7.circ as structural Verilog: 5 circuits, main circuit main
module main (
  input  a,
  input  b,
  input  sel,
  output out
);

  wire and_1_out, and_2_out, not_1_out;

  not not_1 (not_1_out, sel);
  and and_1 (and_1_out, a, not_1_out);
  and and_2 (and_2_out, b, sel);
  or or_1 (out, and_1_out, and_2_out);
endmodule

module \_4х_канальный_мультиплексор  (
  input  A0,
  input  A1,
  input  D0,
  input  D1,
  input  D2,
  input  D3,
  output out_7
);

  wire and_1_out, and_2_out, and_3_out, and_4_out, not_1_out, not_2_out;

  not not_1 (not_1_out, A0);
  not not_2 (not_2_out, A1);
  and and_1 (and_1_out, not_1_out, not_2_out, D0);
  and and_2 (and_2_out, A0, not_2_out, D1);
  and and_3 (and_3_out, not_1_out, A1, D2, A0);
  and and_4 (and_4_out, A0, D3, A1);
  or or_1 (out_7, and_1_out, and_2_out, and_3_out, and_4_out);
endmodule

module \_16ти_канальный_мультиплексор  (
  input  D0,
  input  D1,
  input  D2,
  input  D3,
  input  D4,
  input  D5,
  input  D6,
  input  D7,
  input  D8,
  input  D9,
  input  D10,
  input  D11,
  input  D12,
  input  D13,
  input  D14,
  input  D15,
  input  A0,
  input  A1,
  input  A2,
  input  A3,
  output out_21
);

  wire \n4х_канальный_мультиплексор_1_out_7 , \n4х_канальный_мультиплексор_2_out_7 ,
       \n4х_канальный_мультиплексор_3_out_7 , \n4х_канальный_мультиплексор_4_out_7 ;

  \_4х_канальный_мультиплексор  \u_4х_канальный_мультиплексор_1  (
    .A0(A0), .A1(A1), .D0(D0), .D1(D1), .D2(D2), .D3(D3), .out_7(\n4х_канальный_мультиплексор_1_out_7 ));
  \_4х_канальный_мультиплексор  \u_4х_канальный_мультиплексор_2  (
    .A0(A0), .A1(A1), .D0(D4), .D1(D5), .D2(D6), .D3(D7), .out_7(\n4х_канальный_мультиплексор_2_out_7 ));
  \_4х_канальный_мультиплексор  \u_4х_канальный_мультиплексор_3  (
    .A0(A0), .A1(A1), .D0(D8), .D1(D9), .D2(D10), .D3(D11), .out_7(\n4х_канальный_мультиплексор_3_out_7 ));
  \_4х_канальный_мультиплексор  \u_4х_канальный_мультиплексор_4  (
    .A0(A0), .A1(A1), .D0(D12), .D1(D13), .D2(D14), .D3(D15), .out_7(\n4х_канальный_мультиплексор_4_out_7 ));
  \_4х_канальный_мультиплексор  \u_4х_канальный_мультиплексор_5  (
    .A0(A2), .A1(A3), .D0(\n4х_канальный_мультиплексор_1_out_7 ), .D1(\n4х_канальный_мультиплексор_2_out_7 ),
    .D2(\n4х_канальный_мультиплексор_3_out_7 ), .D3(\n4х_канальный_мультиплексор_4_out_7 ), .out_7(out_21));
endmodule

module \Демультиплексор  (
  input  in_1,
  input  in_2,
  output out_3,
  output out_4
);

  wire not_1_out;

  not not_1 (not_1_out, in_2);
  and and_1 (out_3, in_1, not_1_out);
  and and_2 (out_4, in_1, in_2);
endmodule

module \_16ти_канальный_мультиплесор_с_LOGISIM  (
  input  D0,
  input  D1,
  input  D2,
  input  D3,
  input  D4,
  input  D5,
  input  D6,
  input  D7,
  input  D8,
  input  D9,
  input  D10,
  input  D11,
  input  D12,
  input  D13,
  input  D14,
  input  D15,
  input  A0,
  input  A1,
  input  A2,
  input  A3,
  output out_21
);

  wire multiplexer_1_out, multiplexer_2_out, multiplexer_3_out, multiplexer_4_out;

  Multiplexer #(.select(3)) multiplexer_1 (
    .in0(A0), .in1(A1), .in4(D0), .in5(D1), .in6(D2), .in7(D3), .out(multiplexer_1_out));  // open: in2, in3, sel
  Multiplexer #(.select(3)) multiplexer_2 (
    .in0(A0), .in1(A1), .in2(D4), .in3(D5), .in4(D6), .in5(D7), .out(multiplexer_2_out));  // open: in6, in7, sel
  Multiplexer #(.select(3)) multiplexer_3 (
    .in0(A0), .in1(A1), .in2(D8), .in3(D9), .in4(D10), .in5(D11), .out(multiplexer_3_out));  // open: in6, in7, sel
  Multiplexer #(.select(3)) multiplexer_4 (
    .in0(A0), .in1(A1), .in2(D12), .in3(D13), .in4(D14), .in5(D15), .out(multiplexer_4_out));  // open: in6, in7, sel
  Multiplexer #(.select(3)) multiplexer_5 (
    .in0(A2), .in1(A3), .in2(multiplexer_1_out), .in3(multiplexer_2_out), .in4(multiplexer_3_out),
    .in5(multiplexer_4_out), .out(out_21));  // open: in6, in7, sel
endmodule
