// Logisim project 8LAB.circ as structural Verilog
module \Гарвардская_архитектура  (
);

  wire and_1_out, and_2_out, NUMBER_out, or_1_out, RESET_out;
  wire [7:0] adder_1_out, counter_1_q, multiplexer_1_out, ram_1_data, ram_2_data, register_1_q;

  Button NUMBER (.out(NUMBER_out));
  Button RESET (.out(RESET_out));
  Counter counter_1 (.Q(counter_1_q), .clk(NUMBER_out), .clr(RESET_out));  // open: load, D, count, carry
  RAM ram_1 (.addr(counter_1_q), .data(ram_1_data));  // open: sel, clk, ld, clr
  and and_1 (and_1_out, ram_1_data[0], NUMBER_out);
  RAM #(.bus("separate")) ram_2 (
    .addr(counter_1_q), .din(register_1_q), .data(ram_2_data));  // open: str, sel, clk, ld, clr
  Adder adder_1 (.a(register_1_q), .b(ram_2_data), .out(adder_1_out));  // open: cin, cout
  and and_2 (and_2_out, ram_1_data[1], NUMBER_out);
  // Probe on adder_1_out
  // Probe on register_1_q
  // Probe on multiplexer_1_out
  Multiplexer #(.width(8)) multiplexer_1 (
    .in0(adder_1_out), .in1(ram_2_data), .out(multiplexer_1_out), .sel(ram_1_data[0]));
  Register register_1 (.D(multiplexer_1_out), .Q(register_1_q), .clk(or_1_out));  // open: en, clr
  or or_1 (or_1_out, and_2_out, and_1_out);
endmodule
